# Fritzing sketch Aufbau (saved by Fritzing 0.9.2b)

parts:
  Bauteil1 = Arduino Uno (Rev3) - ICSP  # not connected
  Raspberry_Pi_1 = Raspberry Pi 3 [part_number=RPI-3-V1.2]
  J1 = Basic Servo

nets:
  N1: Raspberry_Pi_1.GIPO18, J1.pulse
  GND: Raspberry_Pi_1.GND, J1.gnd
  5V: Raspberry_Pi_1.5V, J1.vcc
